# Fritzing sketch fritzing_layout (saved by Fritzing 0.9.3b)
breadboards: 1

parts:
  Part1 = Arduino Uno (Rev3)
  LED1 = LED - 3mm [color="Red (633nm)" package="3 mm [THT]"]
  LED2 = LED - 3mm [color="Orange (605nm)" package="3 mm [THT]"]
  LED3 = LED - 3mm [color="White (6500K)" package="3 mm [THT]"]
  LED4 = LED - 3mm [color="Red (633nm)" package="3 mm [THT]"]
  LED5 = LED - 3mm [color="Orange (605nm)" package="3 mm [THT]"]
  LED6 = LED - 3mm [color="White (6500K)" package="3 mm [THT]"]
  R1 = Resistor [tolerance=±5% resistance=220 package=THT]
  R2 = Resistor [tolerance=±5% resistance=220 package=THT]
  R3 = Resistor [tolerance=±5% resistance=220 package=THT]
  R5 = Resistor [tolerance=±5% resistance=220 package=THT]
  S1 = Pushbutton [package="[THT]"]
  R6 = Resistor [tolerance=±5% resistance=220 package=THT]
  Part2 = Thumb Joystick
  hc-sr1 = hc-sr04
  R7 = Rotary Potentiometer (Small) [maximum_resistance=100kΩ package=THT]
  Q1 = NPN-Transistor [package="SOT-23 [SMD]"]
  R8 = Resistor [tolerance=±5% resistance=330 package=THT]
  D1 = Rectifier Diode [part_number=1N4001 package="Melf DO-213 AB [SMD]"]
  M1 = DC Motor
  J1 = Piezo Speaker

nets:
  N1: Part1.A0, Part2.HORZ
  N2: Part1.A1, Part2.VERT
  N3: Part1.A2, R7.wiper
  N4: Part1.D8, R5.Pin_1
  N5: Part1.D9_PWM, R2.Pin_1
  N6: Part1.D11_PWM/MOSI, hc-sr1.Echo
  N7: Part1.D12/MISO, hc-sr1.Trig
  N8: Part1.D13/SCK, Part2.SEL
  N9: Part1.D2, J1.pin1
  N10: Part1.D4, S1.Pin_1, S1.Pin_2, R6.Pin_1
  N11: Part1.D5_PWM, R1.Pin_1
  N12: Part1.D7, R3.Pin_1
  VCC: Part1.5V, S1.Pin_3, S1.Pin_4, Part2.VCC, hc-sr1.VCC, R7.leg2, R8.Pin_0, D1.anode, M1.pin_1
  GND: Part1.GND, LED1.cathode, LED2.cathode, LED3.cathode, LED4.cathode, LED5.cathode, LED6.cathode, R6.Pin_0, Part2.GND, hc-sr1.GND, R7.leg1, Q1.1, J1.pin2
  N13: LED1.anode, LED4.anode, R1.Pin_0
  N14: LED2.anode, R2.Pin_0
  N15: LED3.anode, LED6.anode, R3.Pin_0
  N16: LED5.anode, R5.Pin_0
  N17: Q1.2, D1.cathode, M1.pin_2
  N18: Q1.0, R8.Pin_1
